# Fritzing sketch lesson6-button_switch_module (saved by Fritzing 0.9.9b)
breadboards: 1

parts:
  Componente1 = Arduino Uno (Rev3)
  Part1 = KY-004 Key Switch Module [package="Breakout board"]

nets:
  N1: Componente1.D3_PWM, Part1.S
  5V: Componente1.5V, Part1.Vin
  N2: Componente1.GND, Part1.-

custom parts:
  KY-004 Key Switch Module: Arduino Key Switch Module Keyes KY-004 is a push button that will output a high signal when pressed.

// code stored in the sketch: lesson6-code.ino
// URL: https://arduinomodules.info/ky-004-key-switch-module/

int led = 13; //Define the LED pin
int buttonpin = 3; //Define the push button pin
int val; //Define a numeric variable

void setup()
{
	pinMode(led,OUTPUT);
	pinMode(buttonpin,INPUT);
}

void loop()
{
	val = digitalRead(buttonpin); // check the state of the button
	if(val==HIGH) // if button is pressed, turn LED on
	{
		digitalWrite(led,HIGH);
	}
	else
	{
		digitalWrite(led,LOW);
	}
}
