# Fritzing sketch esp32-button_switch (saved by Fritzing 0.9.9b)
breadboards: 1

parts:
  Part1 = KY-004 Key Switch Module [package="Breakout board"]
  U1 = ESP32S-HiLetgo [part_number=ESP32S-HiLetgo]

nets:
  N1: Part1.S, U1.GPIO23
  N2: Part1.Vin, U1.3.3
  N3: Part1.-, U1.GND

custom parts:
  KY-004 Key Switch Module: Arduino Key Switch Module Keyes KY-004 is a push button that will output a high signal when pressed.
  ESP32S-HiLetgo: HiLetgo ESP-WROOM-32 ESP32 ESP-32S Development Board 2.4GHz Dual-Mode WiFi + Bluetooth Dual Cores Microcontroller The ESP32 integrated with Antenna switches, RF Balun, power amplifiers, low-noise amplifiers, filters, and management modules, and the entire solution occupies the least area of PCB. 2.4 GHz Wi-Fi plus Bluetooth dual-mode chip, with TSMC Ultra-low power consumption 40nm technology,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

// code stored in the sketch: lesson6-code.ino
// URL: https://arduinomodules.info/ky-004-key-switch-module/

int led = 13; //Define the LED pin
int buttonpin = 3; //Define the push button pin
int val; //Define a numeric variable

void setup()
{
	pinMode(led,OUTPUT);
	pinMode(buttonpin,INPUT);
}

void loop()
{
	val = digitalRead(buttonpin); // check the state of the button
	if(val==HIGH) // if button is pressed, turn LED on
	{
		digitalWrite(led,HIGH);
	}
	else
	{
		digitalWrite(led,LOW);
	}
}
