# Fritzing sketch lesson23-joystick_module (saved by Fritzing 0.9.9b)

parts:
  Part1 = KY-023 Dual Axis Joystick Module [package="Breakout board"]
  Componente1 = Arduino Uno (Rev3)

nets:
  GND: Part1.GND, Componente1.GND
  +5V: Part1.+5V, Componente1.5V
  N1: Part1.VRx, Componente1.A0
  N2: Part1.VRy, Componente1.A1
  N3: Part1.SW, Componente1.D7

custom parts:
  KY-023 Dual Axis Joystick Module: X/Y Analog Joystick KEYES KY-023 module. It contains two potentiometers and a button.

// code stored in the sketch: lesson23_code.ino
int sensorPin = 5;
int value = 0; 

void setup() {
  pinMode(3, OUTPUT); 
  Serial.begin(9600);
}

void loop() {
  value = analogRead(0); 
  Serial.print("X:");
  Serial.print(value, DEC); 
  value = analogRead(1); 
  Serial.print(" | Y:"); 
  Serial.print(value, DEC); 
  value = digitalRead(7);
  Serial.print(" | Z: "); 
  Serial.println(value, DEC); 
  delay(100);
}
