# Fritzing sketch esp32-joystick_module (saved by Fritzing 0.9.9b)

parts:
  Part1 = KY-023 Dual Axis Joystick Module [package="Breakout board"]
  U1 = ESP32S-HiLetgo [part_number=ESP32S-HiLetgo]

nets:
  GND: Part1.GND, U1.GND
  N1: Part1.+5V, U1.3.3
  N2: Part1.VRx, U1.GPIO2
  N3: Part1.VRy, U1.GPIO4
  N4: Part1.SW, U1.GPIO15

custom parts:
  KY-023 Dual Axis Joystick Module: X/Y Analog Joystick KEYES KY-023 module. It contains two potentiometers and a button.
  ESP32S-HiLetgo: HiLetgo ESP-WROOM-32 ESP32 ESP-32S Development Board 2.4GHz Dual-Mode WiFi + Bluetooth Dual Cores Microcontroller The ESP32 integrated with Antenna switches, RF Balun, power amplifiers, low-noise amplifiers, filters, and management modules, and the entire solution occupies the least area of PCB. 2.4 GHz Wi-Fi plus Bluetooth dual-mode chip, with TSMC Ultra-low power consumption 40nm technology,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

// code stored in the sketch: lesson23_code.ino
int sensorPin = 5;
int value = 0; 

void setup() {
  pinMode(3, OUTPUT); 
  Serial.begin(9600);
}

void loop() {
  value = analogRead(0); 
  Serial.print("X:");
  Serial.print(value, DEC); 
  value = analogRead(1); 
  Serial.print(" | Y:"); 
  Serial.print(value, DEC); 
  value = digitalRead(7);
  Serial.print(" | Z: "); 
  Serial.println(value, DEC); 
  delay(100);
}
