# Fritzing sketch lesson15-light_dependent_resistor_module (saved by Fritzing 0.9.9b)
breadboards: 1

parts:
  Part1 = KY-018 Photoresistor Module [package="Breakout board"]
  Componente1 = Arduino Uno (Rev3)

nets:
  N1: Part1.S, Componente1.A0
  VIN: Part1.Vin, Componente1.5V
  N2: Part1.-, Componente1.GND

custom parts:
  KY-018 Photoresistor Module: KY-018 Photoresistor module, used to measure light intensity. It can determine the presence or absence of light.

// code stored in the sketch: lesson15-code.ino
int sensorPin = A0; // select the input pin for the potentiometer 
int ledPin = 13; // select the pin for the LED
int sensorValue = 0; // variable to store the value coming from the sensor 

void setup() {
  pinMode(ledPin, OUTPUT); 
  Serial.begin(9600);
}

void loop() {
  sensorValue = analogRead(sensorPin);
  digitalWrite(ledPin, HIGH); 
  delay(sensorValue); 
  digitalWrite(ledPin, LOW); 
  delay(sensorValue); 
  Serial.println(sensorValue, DEC);
}
