# Fritzing sketch esp32-light_dependent_resistor_module (saved by Fritzing 0.9.9b)
breadboards: 1

parts:
  Part1 = KY-018 Photoresistor Module [package="Breakout board"]
  U1 = ESP32S-HiLetgo [part_number=ESP32S-HiLetgo]

nets:
  N1: Part1.S, U1.GPIO15
  N2: Part1.Vin, U1.3.3
  N3: Part1.-, U1.GND

custom parts:
  KY-018 Photoresistor Module: KY-018 Photoresistor module, used to measure light intensity. It can determine the presence or absence of light.
  ESP32S-HiLetgo: HiLetgo ESP-WROOM-32 ESP32 ESP-32S Development Board 2.4GHz Dual-Mode WiFi + Bluetooth Dual Cores Microcontroller The ESP32 integrated with Antenna switches, RF Balun, power amplifiers, low-noise amplifiers, filters, and management modules, and the entire solution occupies the least area of PCB. 2.4 GHz Wi-Fi plus Bluetooth dual-mode chip, with TSMC Ultra-low power consumption 40nm technology,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

// code stored in the sketch: lesson15-code.ino
int sensorPin = A0; // select the input pin for the potentiometer 
int ledPin = 13; // select the pin for the LED
int sensorValue = 0; // variable to store the value coming from the sensor 

void setup() {
  pinMode(ledPin, OUTPUT); 
  Serial.begin(9600);
}

void loop() {
  sensorValue = analogRead(sensorPin);
  digitalWrite(ledPin, HIGH); 
  delay(sensorValue); 
  digitalWrite(ledPin, LOW); 
  delay(sensorValue); 
  Serial.println(sensorValue, DEC);
}
