# Fritzing sketch arduino_reel_digital (saved by Fritzing 0.9.9b)

parts:
  Mod1 = KY-021 Mini Magnetic Reed Switch Module [package="Breakout board"]
  Componente1 = Arduino Uno (Rev3)

nets:
  N1: Mod1.S, Componente1.D2
  VIN: Mod1.Vin, Componente1.5V
  N2: Mod1.-, Componente1.GND

custom parts:
  KY-021 Mini Magnetic Reed Switch Module: KY-021 magnetic reed switch module. A reed switch is a magnetic sensor that is normally open and gets closed when exposed to a magnetic field.
