# Fritzing sketch arduino_ultrasonido (saved by Fritzing 0.9.9b)

parts:
  HC-SR04_Sensor_1 = HC-SR04 Ultrasonic Distance Sensor
  Componente1 = Arduino Uno (Rev3)

nets:
  VCC: HC-SR04_Sensor_1.VCC, Componente1.5V
  N1: HC-SR04_Sensor_1.TRIG, Componente1.D7
  N2: HC-SR04_Sensor_1.ECHO, Componente1.D8
  GND: HC-SR04_Sensor_1.GND, Componente1.GND
