# Fritzing sketch arduino_ultrasonido2 (saved by Fritzing 0.9.9b)

parts:
  HC-SR04_Sensor_1 = HC-SR04 Ultrasonic Distance Sensor
  Componente1 = Arduino Uno (Rev3)
  Part2 = KY-016 RGB Full Color LED Module [package="Breakout board"]

nets:
  VCC: HC-SR04_Sensor_1.VCC, Componente1.5V
  N1: HC-SR04_Sensor_1.TRIG, Componente1.D11_PWM/MOSI
  N2: HC-SR04_Sensor_1.ECHO, Componente1.D12/MISO
  GND: HC-SR04_Sensor_1.GND, Componente1.GND, Part2.-
  N3: Componente1.D3_PWM, Part2.R
  N4: Componente1.D5_PWM, Part2.G
  N5: Componente1.D6_PWM, Part2.B

custom parts:
  KY-016 RGB Full Color LED Module: KY-016 Arduino full color 5mm RGB LED, different colors can be obtained by mixing the three primary colors.
