# Fritzing sketch arduino_ultrasonido3 (saved by Fritzing 0.9.9b)
breadboards: 1

parts:
  HC-SR04_Sensor_1 = HC-SR04 Ultrasonic Distance Sensor
  Componente1 = Arduino Uno (Rev3)
  Part2 = KY-016 RGB Full Color LED Module [package="Breakout board"]
  Part3 = KY-006 Passive Buzzer Module [package="Breakout board"]
  J1 = Basic Servo

nets:
  VCC: HC-SR04_Sensor_1.VCC, Componente1.5V, J1.vcc
  N1: HC-SR04_Sensor_1.TRIG, Componente1.D11_PWM/MOSI
  N2: HC-SR04_Sensor_1.ECHO, Componente1.D12/MISO
  GND: HC-SR04_Sensor_1.GND, Componente1.GND, Part2.-, Part3.-, J1.gnd
  N3: Componente1.D9_PWM, J1.pulse
  N4: Componente1.D10_PWM/SS, Part3.S
  N5: Componente1.D3_PWM, Part2.R
  N6: Componente1.D5_PWM, Part2.G
  N7: Componente1.D6_PWM, Part2.B

custom parts:
  KY-016 RGB Full Color LED Module: KY-016 Arduino full color 5mm RGB LED, different colors can be obtained by mixing the three primary colors.
  KY-006 Passive Buzzer Module: Passive Piezoelectric Buzzer Module Keyes KY-006, it can produce a range of sound tones depending on the input frequency.
