# Fritzing sketch esp32_ultrasonido (saved by Fritzing 0.9.9b)

parts:
  HC-SR04_Sensor_1 = HC-SR04 Ultrasonic Distance Sensor
  U1 = ESP32S-HiLetgo [part_number=ESP32S-HiLetgo]

nets:
  VCC: HC-SR04_Sensor_1.VCC, U1.VIN
  N1: HC-SR04_Sensor_1.TRIG, U1.GPIO5
  N2: HC-SR04_Sensor_1.ECHO, U1.GPIO18
  GND: HC-SR04_Sensor_1.GND, U1.GND

custom parts:
  ESP32S-HiLetgo: HiLetgo ESP-WROOM-32 ESP32 ESP-32S Development Board 2.4GHz Dual-Mode WiFi + Bluetooth Dual Cores Microcontroller The ESP32 integrated with Antenna switches, RF Balun, power amplifiers, low-noise amplifiers, filters, and management modules, and the entire solution occupies the least area of PCB. 2.4 GHz Wi-Fi plus Bluetooth dual-mode chip, with TSMC Ultra-low power consumption 40nm technology,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
